// Logisim project calculator.circ as structural Verilog: 1 circuit, main circuit main
module main (
  input  in_1,
  input  in_2,
  input  in_3,
  input  in_4,
  input  in_5,
  input  in_6,
  input  in_7,
  input  in_8,
  input  in_9,
  input  in_10,
  input  in_11,
  input  in_12,
  input  in_13,
  input  in_14,
  input  in_15,
  input  in_16,
  input  in_17,
  input  in_18,
  input  in_19,
  input  in_20,
  input  in_21,
  input  in_22,
  input  in_23,
  input  in_24,
  input  in_25,
  input  in_26,
  input  in_27,
  input  in_28,
  input  in_29,
  input  in_30,
  input  in_31,
  input  in_32,
  input  in_33,
  input  in_34,
  input  in_35,
  input  in_36,
  input  in_37,
  input  in_38,
  input  in_39,
  input  in_40,
  input  in_41,
  input  in_42,
  input  in_43,
  input  in_44,
  input  in_45,
  input  in_46,
  input  in_47,
  input  in_48
);

  wire main_1_out_13, main_2_p1, main_2_p2, main_2_p3, main_2_p4, main_2_p5, main_2_p6, main_2_p7, main_2_p8,
       main_2_p9, main_2_p10, main_2_p11, main_2_p12, main_3_out_13, main_3_out_14, main_3_out_15,
       main_3_out_16, main_3_out_17, main_3_out_18, main_3_out_19, main_4_out_13, main_4_out_14,
       main_4_out_15, main_4_out_16, main_4_out_17, main_4_out_18;

  LED led_1 (.in(main_1_out_13));
  a_greater_than_b_main main_1 (
    .in_1(in_1), .in_2(in_2), .in_3(in_3), .in_4(in_4), .in_5(in_5), .in_6(in_6), .in_7(in_19), .in_8(in_20),
    .in_9(in_21), .in_10(in_22), .in_11(in_23), .in_12(in_24), .out_13(main_1_out_13));
  LED led_2 (.in(main_2_p5));
  LED led_3 (.in(main_2_p3));
  LED led_4 (.in(main_2_p1));
  LED led_5 (.in(main_2_p7));
  LED led_6 (.in(main_2_p8));
  LED led_7 (.in(main_2_p4));
  LED led_8 (.in(main_2_p2));
  LED led_9 (.in(main_2_p6));
  LED led_10 (.in(main_2_p9));
  LED led_11 (.in(main_2_p11));
  // division_main main_2: pin names not known; wires that end beside it: main_2_p1, main_2_p2, main_2_p3, main_2_p4, main_2_p5, main_2_p6, main_2_p7, main_2_p8, main_2_p9, main_2_p10, main_2_p11, main_2_p12, in_37, in_43
  LED led_12 (.in(main_2_p10));
  LED led_13 (.in(main_2_p12));
  LED led_14 (.in(main_3_out_14));
  LED led_15 (.in(main_3_out_13));
  LED led_16 (.in(main_3_out_15));
  LED led_17 (.in(main_3_out_18));
  LED led_18 (.in(main_3_out_16));
  LED led_19 (.in(main_3_out_17));
  LED led_20 (.in(main_3_out_19));
  addition_main main_3 (
    .in_1(in_7), .in_2(in_8), .in_3(in_9), .in_4(in_10), .in_5(in_11), .in_6(in_12), .in_7(in_25),
    .in_8(in_26), .in_9(in_27), .in_10(in_28), .in_11(in_29), .in_12(in_30), .out_13(main_3_out_13),
    .out_14(main_3_out_14), .out_15(main_3_out_15), .out_16(main_3_out_16), .out_17(main_3_out_17),
    .out_18(main_3_out_18), .out_19(main_3_out_19));
  LED led_21 (.in(main_4_out_18));
  LED led_22 (.in(main_4_out_16));
  LED led_23 (.in(main_4_out_17));
  LED led_24 (.in(main_4_out_15));
  LED led_25 (.in(main_4_out_13));
  LED led_26 (.in(main_4_out_14));
  subtraction_main main_4 (
    .in_7(in_31), .in_8(in_32), .in_9(in_33), .in_10(in_34), .in_11(in_35), .in_12(in_36),
    .out_15(main_4_out_15), .out_16(main_4_out_16), .out_17(main_4_out_17), .out_18(main_4_out_18),
    .in_1(in_13), .in_2(in_14), .in_3(in_15), .in_4(in_16), .in_5(in_17), .in_6(in_18),
    .out_13(main_4_out_13), .out_14(main_4_out_14));
endmodule
