// Logisim project rudimentary computing device.circ as structural Verilog: 1 circuit, main circuit main
module main (
  input  [5:0] in_1,
  input  [5:0] in_2,
  input  [5:0] in_3,
  input  in_4,
  output [5:0] out_5,
  output [5:0] out_6,
  output [5:0] out_7
);

  wire button_1_out, clock_1_out, main_2_a_b, main_2_a_b_2, main_2_a_b_3, main_2_add, main_2_insert,
       main_2_invert, main_2_out, main_2_out_14, main_2_step;
  wire [0:0] main_4_equality_check, main_5_out_13, main_6_out_13;
  wire [5:0] and_6_out, main_1_out_14, main_3_out_4, main_7_out_12, main_9_out_19, main_10_out_18,
       main_11_out_10, main_11_out_11, main_11_out_12, main_12_out_18, main_13_out_18, main_14_out_8,
       main_14_out_9, main_14_out_10, main_15_out_8, main_15_out_9, main_15_out_10, main_16_out_8,
       main_16_out_9, main_16_out_10, main_17_out_8, main_17_out_9, main_17_out_10, main_18_out_8,
       main_18_out_9, main_18_out_10, main_19_out_8, main_19_out_9, main_19_out_10, main_20_out_8,
       main_20_out_9, main_20_out_10, main_21_out_8, main_21_out_9, main_21_out_10;
  wire [5:1] rom_1_data_2;
  wire [18:5] rom_1_data;

  Clock clock_1 (.out(clock_1_out));
  LED led_1 (.in(main_1_out_14[5]));
  LED led_2 (.in(main_1_out_14[4]));
  Button button_1 (.out(button_1_out));
  LED led_3 (.in(main_1_out_14[3]));
  LED led_4 (.in(main_1_out_14[2]));
  LED led_5 (.in(main_1_out_14[0]));
  LED led_6 (.in(main_1_out_14[1]));
  program_counter_main main_1 (
    .in_7(button_1_out), .in_8(clock_1_out), .out_9(main_1_out_14[5]), .out_10(main_1_out_14[4]),
    .out_11(main_1_out_14[3]), .out_12(main_1_out_14[2]), .out_13(main_1_out_14[1]),
    .out_14(main_1_out_14[0]), .in_1(and_6_out[5]), .in_2(and_6_out[4]), .in_3(and_6_out[3]),
    .in_4(and_6_out[2]), .in_5(and_6_out[1]), .in_6(and_6_out[0]));
  instructor_main main_2 (
    .in_1(rom_1_data[18]), .in_2(rom_1_data[17]), .in_3(rom_1_data[16]), .in_4(rom_1_data[15]),
    .ADD(main_2_add), .INVERT(main_2_invert), .A_B(main_2_a_b), .A_B_2(main_2_a_b_2), .A_B_3(main_2_a_b_3),
    .STEP(main_2_step), .INSERT(main_2_insert), .OUT(main_2_out), .out_14(main_2_out_14));  // open: HALT, out_15, out_16
  step_selector_main main_3 (
    .in_2(main_13_out_18[0]), .in_1(main_10_out_18), .in_3(main_12_out_18), .out_4(main_3_out_4));
  equality_check_main main_4 (
    .Equality_Check(main_4_equality_check[0]), .in_1(main_10_out_18[5]), .in_2(main_10_out_18[4]),
    .Number_A(main_10_out_18[3]), .in_4(main_10_out_18[2]), .in_5(main_10_out_18[1]),
    .in_6(main_10_out_18[0]), .in_7(main_12_out_18[5]), .in_8(main_12_out_18[4]), .in_9(main_12_out_18[3]),
    .in_10(main_12_out_18[2]), .in_11(main_12_out_18[1]), .in_12(main_12_out_18[0]));
  a_less_than_b_main main_5 (
    .in_7(main_12_out_18[5]), .in_8(main_12_out_18[4]), .in_9(main_12_out_18[3]), .in_10(main_12_out_18[2]),
    .in_11(main_12_out_18[1]), .in_12(main_12_out_18[0]), .in_1(main_10_out_18[5]), .in_2(main_10_out_18[4]),
    .in_3(main_10_out_18[3]), .in_4(main_10_out_18[2]), .in_5(main_10_out_18[1]), .in_6(main_10_out_18[0]),
    .out_13(main_5_out_13[0]));
  a_greater_than_b_main main_6 (
    .in_1(main_10_out_18[5]), .in_2(main_10_out_18[4]), .in_3(main_10_out_18[3]), .in_4(main_10_out_18[2]),
    .in_5(main_10_out_18[1]), .in_6(main_10_out_18[0]), .in_7(main_12_out_18[5]), .in_8(main_12_out_18[4]),
    .in_9(main_12_out_18[3]), .in_10(main_12_out_18[2]), .in_11(main_12_out_18[1]),
    .in_12(main_12_out_18[0]), .out_13(main_6_out_13[0]));
  inverter_main main_7 (
    .in_1(main_10_out_18[5]), .in_2(main_10_out_18[4]), .in_3(main_10_out_18[3]), .in_4(main_10_out_18[2]),
    .in_5(main_10_out_18[1]), .in_6(main_10_out_18[0]), .out_7(main_7_out_12[5]), .out_8(main_7_out_12[4]),
    .out_9(main_7_out_12[3]), .out_10(main_7_out_12[2]), .out_11(main_7_out_12[1]), .out_12(main_7_out_12[0]));
  input_selector_main main_8 (
    .in_4(main_2_out), .in_1({6{1'b0}}), .in_2({6{1'b0}}), .in_3({6{1'b0}}), .in_5(main_10_out_18),
    .in_6(main_12_out_18), .in_7(main_13_out_18), .out_8(out_5), .out_9(out_6), .out_10(out_7));
  addition_main main_9 (
    .in_1(main_12_out_18[5]), .in_2(main_12_out_18[4]), .in_3(main_12_out_18[3]), .in_4(main_12_out_18[2]),
    .in_5(main_12_out_18[1]), .in_6(main_12_out_18[0]), .in_7(main_10_out_18[5]), .in_8(main_10_out_18[4]),
    .in_9(main_10_out_18[3]), .in_10(main_10_out_18[2]), .in_11(main_10_out_18[1]),
    .in_12(main_10_out_18[0]), .out_14(main_9_out_19[5]), .out_15(main_9_out_19[4]),
    .out_16(main_9_out_19[3]), .out_17(main_9_out_19[2]), .out_18(main_9_out_19[1]), .out_19(main_9_out_19[0]));  // open: out_13
  ROM #(.addrWidth(6), .dataWidth(19)) rom_1 (.addr(main_1_out_14), .data({rom_1_data, rom_1_data_2}));  // open: sel
  memory_main main_10 (
    .Address(main_21_out_8[5]), .in_2(main_21_out_8[4]), .Write(main_21_out_8[3]), .in_4(main_21_out_8[2]),
    .Read(main_21_out_8[1]), .Initialise(button_1_out), .in_7(main_20_out_8[5]), .in_8(main_20_out_8[4]),
    .Input(main_20_out_8[3]), .in_10(main_20_out_8[2]), .in_11(main_20_out_8[1]), .in_12(main_20_out_8[0]),
    .out_13(main_10_out_18[5]), .out_14(main_10_out_18[4]), .Output(main_10_out_18[3]),
    .out_16(main_10_out_18[2]), .out_17(main_10_out_18[1]), .out_18(main_10_out_18[0]));
  and and_1 (and_6_out[5], main_3_out_4[5], main_2_step);
  ram_value_transfer_main main_11 (
    .in_1(main_21_out_8), .in_2(main_12_out_18), .out_10(main_11_out_10), .in_3(main_10_out_18),
    .in_4(main_21_out_9), .in_5(main_13_out_18), .out_11(main_11_out_11), .in_6(main_12_out_18),
    .in_7(main_21_out_10), .in_8(main_10_out_18), .out_12(main_11_out_12), .in_9(main_13_out_18));
  and and_2 (and_6_out[4], main_3_out_4[4], main_2_step);
  and and_3 (and_6_out[3], main_3_out_4[3], main_2_step);
  and and_4 (and_6_out[2], main_3_out_4[2], main_2_step);
  memory_main main_12 (
    .Address(main_21_out_9[5]), .in_2(main_21_out_9[4]), .Write(main_21_out_9[3]), .in_4(main_21_out_9[2]),
    .Read(main_21_out_9[1]), .Initialise(button_1_out), .in_7(main_20_out_9[5]), .in_8(main_20_out_9[4]),
    .Input(main_20_out_9[3]), .in_10(main_20_out_9[2]), .in_11(main_20_out_9[1]), .in_12(main_20_out_9[0]),
    .out_13(main_12_out_18[5]), .out_14(main_12_out_18[4]), .Output(main_12_out_18[3]),
    .out_16(main_12_out_18[2]), .out_17(main_12_out_18[1]), .out_18(main_12_out_18[0]));
  and and_5 (and_6_out[1], main_3_out_4[1], main_2_step);
  and and_6 (and_6_out[0], main_3_out_4[0], main_2_step);
  memory_main main_13 (
    .Address(main_21_out_10[5]), .in_2(main_21_out_10[4]), .Write(main_21_out_10[3]),
    .in_4(main_21_out_10[2]), .Read(main_21_out_10[1]), .Initialise(button_1_out), .in_7(main_20_out_10[5]),
    .in_8(main_20_out_10[4]), .Input(main_20_out_10[3]), .in_10(main_20_out_10[2]),
    .in_11(main_20_out_10[1]), .in_12(main_20_out_10[0]), .out_13(main_13_out_18[5]),
    .out_14(main_13_out_18[4]), .Output(main_13_out_18[3]), .out_16(main_13_out_18[2]),
    .out_17(main_13_out_18[1]), .out_18(main_13_out_18[0]));
  input_selector_main main_14 (
    .in_4(main_2_out_14), .in_1({6{1'b0}}), .in_2({6{1'b0}}), .in_3({6{1'b0}}), .in_5(main_11_out_11),
    .in_6(main_11_out_12), .in_7(main_11_out_10), .out_8(main_14_out_8), .out_9(main_14_out_9),
    .out_10(main_14_out_10));
  input_selector_main main_15 (
    .in_4(main_2_a_b_3), .in_1(main_14_out_8), .in_2(main_14_out_9), .in_3(main_14_out_10), .in_5({6{1'b0}}),
    .in_6({6{1'b0}}), .in_7({{5{1'b0}}, main_4_equality_check[0]}), .out_8(main_15_out_8),
    .out_9(main_15_out_9), .out_10(main_15_out_10));
  input_selector_main main_16 (
    .in_4(main_2_a_b_2), .in_1(main_15_out_8), .in_2(main_15_out_9), .in_3(main_15_out_10), .in_5({6{1'b0}}),
    .in_6({6{1'b0}}), .in_7({{5{1'b0}}, main_5_out_13[0]}), .out_8(main_16_out_8), .out_9(main_16_out_9),
    .out_10(main_16_out_10));
  input_selector_main main_17 (
    .in_4(main_2_a_b), .in_1(main_16_out_8), .in_2(main_16_out_9), .in_3(main_16_out_10), .in_5({6{1'b0}}),
    .in_6({6{1'b0}}), .in_7({{5{1'b0}}, main_6_out_13[0]}), .out_8(main_17_out_8), .out_9(main_17_out_9),
    .out_10(main_17_out_10));
  input_selector_main main_18 (
    .in_4(main_2_invert), .in_1(main_17_out_8), .in_2(main_17_out_9), .in_3(main_17_out_10),
    .in_5({6{1'b0}}), .in_6({6{1'b0}}), .in_7(main_7_out_12), .out_8(main_18_out_8), .out_9(main_18_out_9),
    .out_10(main_18_out_10));
  input_selector_main main_19 (
    .in_4(main_2_insert), .in_1(main_18_out_8), .in_2(main_18_out_9), .in_3(main_18_out_10), .in_5(in_1),
    .in_6(in_2), .in_7(in_3), .out_8(main_19_out_8), .out_9(main_19_out_9), .out_10(main_19_out_10));
  input_selector_main main_20 (
    .in_4(main_2_add), .in_1(main_19_out_8), .in_2(main_19_out_9), .in_3(main_19_out_10), .in_5({6{1'b0}}),
    .in_6({6{1'b0}}), .in_7(main_9_out_19), .out_8(main_20_out_8), .out_9(main_20_out_9),
    .out_10(main_20_out_10));
  input_selector_main main_21 (
    .in_4(in_4), .in_1({rom_1_data[14:10], 1'b0}), .in_2({rom_1_data[9:5], 1'b0}),
    .in_3({rom_1_data_2, 1'b0}), .in_5({6{1'b0}}), .in_6({6{1'b0}}), .in_7({6{1'b0}}), .out_8(main_21_out_8),
    .out_9(main_21_out_9), .out_10(main_21_out_10));

  // Notes on the sheet:
  //   contents of rom_1 (hex, n*v repeats v):
  //   0 39800 380c0 194a6 40005 39800 1140a 40009 9 a b c d e f
endmodule
